# Fritzing sketch button_led (saved by Fritzing 0.9.2b)
breadboards: 1

parts:
  R1 = Resistor [tolerance=±5% resistance=100k package=THT]
  Arduino1 = Arduino Uno (Rev3)
  S1 = Pushbutton [package="[THT]"]
  LED1 = LED - 5mm [color="Red (633nm)" package="5 mm [THT]"]

nets:
  N1: R1.Pin_0, Arduino1.D2, S1.Pin_1, S1.Pin_2
  N2: R1.Pin_1, Arduino1.5V
  N3: Arduino1.D13/SCK, LED1.anode
  N4: Arduino1.GND, S1.Pin_3, S1.Pin_4, LED1.cathode
