# Fritzing sketch button_led_pullup (saved by Fritzing 0.9.2b)
breadboards: 1

parts:
  Arduino1 = Arduino Uno (Rev3)
  S1 = Pushbutton [package="[THT]"]
  LED1 = LED - 5mm [color="Red (633nm)" package="5 mm [THT]"]

nets:
  N1: Arduino1.D13/SCK, LED1.anode
  N2: Arduino1.D2, S1.Pin_1, S1.Pin_2
  N3: Arduino1.GND, S1.Pin_3, S1.Pin_4, LED1.cathode
