# Fritzing sketch buz+ultrasonic (saved by Fritzing 0.9.2b)
breadboards: 1

parts:
  Arduino1 = Arduino Uno (Rev3)
  J1 = Infrared Proximity Sensor
  J2 = Piezo Speaker

nets:
  N1: Arduino1.D11_PWM/MOSI, J2.pin2
  N2: Arduino1.D2, J1.Vout
  5V: Arduino1.5V, J1.Vcc
  GND: Arduino1.GND, J1.GND, J2.pin1

notes:
  Trigger : D3
  Echo : D2
