# Fritzing sketch cds (saved by Fritzing 0.9.2b)
breadboards: 1

parts:
  Arduino1 = Arduino Uno (Rev3)
  R1 = Photocell (LDR) [package=THT]
  LED1 = LED - 5mm [color="Red (633nm)" package="5 mm [THT]"]

nets:
  N1: Arduino1.A0, R1.pin_0
  N2: Arduino1.D13/SCK, LED1.anode
  N3: Arduino1.GND, LED1.cathode
  N4: Arduino1.5V, R1.pin_1
