# Fritzing sketch cds_potention (saved by Fritzing 0.9.2b)
breadboards: 1

parts:
  Arduino1 = Arduino Uno (Rev3)
  R1 = Photocell (LDR) [package=THT]
  LED1 = LED - 5mm [color="Red (633nm)" package="5 mm [THT]"]
  R2 = Rotary Potentiometer (Small) [maximum_resistance=100kΩ package=THT]

nets:
  N1: Arduino1.A1, R2.wiper
  N2: Arduino1.D13/SCK, LED1.anode
  N3: Arduino1.GND, R1.pin_1, LED1.cathode, R2.leg2
  N4: Arduino1.5V, R1.pin_0, R2.leg1
