# Fritzing sketch led+potentionmeter (saved by Fritzing 0.9.2b)
breadboards: 1

parts:
  Arduino1 = Arduino Uno (Rev3)
  LED1 = LED - 5mm [color="Red (633nm)" package="5 mm [THT]"]
  R2 = Resistor [tolerance=±5% resistance=220 package=THT]  # not connected
  R3 = Rotary Potentiometer (Small) [maximum_resistance=100kΩ package=THT]

nets:
  N1: Arduino1.A0, R3.wiper
  N2: Arduino1.D11_PWM/MOSI, LED1.anode
  N3: Arduino1.5V, R3.leg1
  N4: Arduino1.GND, R3.leg2
